# Fritzing sketch SvinoBot (saved by Fritzing 0.9.3b)
breadboards: 1

parts:
  Raspberry_Pi_1 = Raspberry Pi 3 [part_number=RPI-3-V1.2]
  LED1 = RGB LED (com. cathode, rgb) [package="5 mm [THT]"]
  Part2 = Breakout Board for Electret Microphone
  R2 = Resistor [tolerance=±5% resistance=150k package=THT]
  R3 = Resistor [tolerance=±5% resistance=150k package=THT]
  R1 = Resistor [tolerance=±5% resistance=150k package=THT]
  Part3 = Adafruit BME280
  PIR1 = PIR sensor
  R4 = Resistor [tolerance=±5% resistance=100k package=THT]
  LED2 = Infrared LED - 5mm [package="5 mm [THT]"]
  Q1 = Basic FET P-Channel [package="D2Pak [SMD]"]
  BATT1 = 4xAA Switchable Battery Pack w/Bare Wire

nets:
  3V3: Raspberry_Pi_1.3v3, Part3.3.3V
  N1: Raspberry_Pi_1.GPIO2, Part3.SDI/SDA, Part3.CS
  N2: Raspberry_Pi_1.GPIO3, Part3.SCK/SCL, Part3.SDO/ADR
  GND: Raspberry_Pi_1.GND, LED1.common_cathode, Part2.GND, Part3.GND, PIR1.GND
  N3: Raspberry_Pi_1.GPIO22, Q1.source
  N4: Raspberry_Pi_1.GPIO5, R1.Pin_1
  N5: Raspberry_Pi_1.GPIO6, R3.Pin_1
  N6: Raspberry_Pi_1.GPIO13, R2.Pin_1
  N7: Raspberry_Pi_1.GPIO26, Part2.AUD
  N8: Raspberry_Pi_1.GPIO24, PIR1.SIG
  N9: Raspberry_Pi_1.GPIO23, PIR1.VDD
  5V: Raspberry_Pi_1.5V, Part2.VCC
  N10: LED1.red_anode, R1.Pin_0
  N11: LED1.green_anode, R4.Pin_1
  N12: LED1.blue_anode, R2.Pin_0
  N13: R3.Pin_0, R4.Pin_0
  N14: LED2.cathode, BATT1.NEG
  N15: LED2.anode, Q1.drain
  N16: Q1.Gate, BATT1.POS

custom parts:
  Adafruit BME280: Bosch has stepped up their game with their new BME280 sensor, an environmental sensor with temperature, barometric pressure and humidity! This sensor is great for all sorts of weather/environmental sensing and can even be used in both I2C and SPI! This precision sensor from Bosch is the best low-cost sensing solution for measuring humidity with ±3% accuracy, barometric pressure with ±1 hPa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
  Infrared LED - 5mm: A generic infrared LED (~1.2V)
  4xAA Switchable Battery Pack w/Bare Wire: 4xAA Switchable Battery Pack with Bare Wire connection
